// Digital circuit cacheIntento.dig as structural Verilog
module cacheIntento (
);

  ROM #(.AddrBits(10), .Bits(32)) CacheMem ();  // open: A, sel, D
  Comparator comparator_1 ();  // open: a, b, gt, eq, lt
  Comparator comparator_2 ();  // open: a, b, gt, eq, lt
  Comparator comparator_3 ();  // open: a, b, gt, eq, lt
endmodule
